// Logisim project ALU.circ as structural Verilog: 1 circuit, main circuit main
module main (
  input  [15:0] A,
  input  [15:0] B,
  input  [3:0] Select_Bits,
  input  [7:0] CCR,
  output [15:0] out_5,
  output [7:0] CCR_O
);

  wire aritmetic_unit_16_bit_1_p5, aritmetic_unit_16_bit_1_p6, aritmetic_unit_16_bit_1_p9, clock_out,
       main_1_p6, main_1_p7, main_2_p4, main_2_p5, main_2_p7;
  wire [4:1] register_1_q;
  wire [15:0] aritmetic_unit_16_bit_1_p7, main_1_p5, main_2_p6, multiplexer_1_out, Register_A_q, Register_B_q;

  Clock clock (.out(clock_out));
  Register #(.width(16)) Register_A (.D(A), .Q(Register_A_q), .clk(clock_out));  // open: en, clr
  Register #(.width(16)) Register_B (.D(B), .Q(Register_B_q), .clk(clock_out));  // open: en, clr
  Register #(.width(4)) register_1 (.D(Select_Bits), .Q(register_1_q), .clk(clock_out));  // open: en, clr
  // logical_unit_main main_1: pin names not known; wires that end beside it: Register_A_q, Register_B_q, register_1_q, CCR[0], main_1_p5, main_1_p6, main_1_p7
  // Probe on main_1_p6
  // Probe on main_1_p7
  // shift_main main_2: pin names not known; wires that end beside it: Register_A_q, register_1_q, CCR[0], main_2_p4, main_2_p5, main_2_p6, main_2_p7
  // Probe on main_2_p7
  // Probe on main_2_p4
  // Probe on main_2_p5
  // Probe on aritmetic_unit_16_bit_1_p5
  // Probe on aritmetic_unit_16_bit_1_p6
  // Aritmetic_Unit_16_bit aritmetic_unit_16_bit_1: pin names not known; wires that end beside it: Register_A_q, Register_B_q, register_1_q, CCR[0], aritmetic_unit_16_bit_1_p5, aritmetic_unit_16_bit_1_p6, aritmetic_unit_16_bit_1_p7, CCR_O[0], aritmetic_unit_16_bit_1_p9
  // Probe on aritmetic_unit_16_bit_1_p9
  Multiplexer #(.select(5), .width(16)) multiplexer_1 (
    .in0(main_2_p6), .in1(main_2_p6), .in2(main_2_p6), .in3(main_2_p6), .in4(main_2_p6), .in5(main_2_p6),
    .in6(main_2_p6), .in8(main_1_p5), .in9(main_1_p5), .in10(main_1_p5), .in11(main_1_p5), .in12(main_1_p5),
    .in13(main_1_p5), .in14(main_1_p5), .in15(main_1_p5), .in16(aritmetic_unit_16_bit_1_p7),
    .in17(aritmetic_unit_16_bit_1_p7), .in18(aritmetic_unit_16_bit_1_p7), .in19(aritmetic_unit_16_bit_1_p7),
    .in20(aritmetic_unit_16_bit_1_p7), .in21(aritmetic_unit_16_bit_1_p7), .in22(aritmetic_unit_16_bit_1_p7),
    .in23(aritmetic_unit_16_bit_1_p7), .in28(aritmetic_unit_16_bit_1_p7), .out(multiplexer_1_out),
    .sel({register_1_q, CCR[0]}));  // open: in7, in24, in25, in26, in27, in29, in30, in31, en
  // Probe on CCR_O[0]
  Register #(.width(16)) register_2 (.D(multiplexer_1_out), .Q(out_5), .clk(clock_out));  // open: en, clr
  Multiplexer #(.select(5)) multiplexer_2 (
    .in0(main_2_p5), .in1(main_2_p5), .in2(main_2_p5), .in3(main_2_p5), .in4(main_2_p5), .in5(main_2_p5),
    .in6(main_2_p5), .in8(main_1_p7), .in9(main_1_p7), .in10(main_1_p7), .in11(main_1_p7), .in12(main_1_p7),
    .in13(main_1_p7), .in14(main_1_p7), .in15(main_1_p7), .in16(aritmetic_unit_16_bit_1_p6),
    .in17(aritmetic_unit_16_bit_1_p6), .in18(aritmetic_unit_16_bit_1_p6), .in19(aritmetic_unit_16_bit_1_p6),
    .in20(aritmetic_unit_16_bit_1_p6), .in21(aritmetic_unit_16_bit_1_p6), .in22(aritmetic_unit_16_bit_1_p6),
    .in23(aritmetic_unit_16_bit_1_p6), .in28(aritmetic_unit_16_bit_1_p6), .out(CCR_O[2]),
    .sel({register_1_q, CCR[0]}));  // open: in7, in24, in25, in26, in27, in29, in30, in31, en
  // Probe on CCR[1]
  // Probe on CCR_O[2]
  // Probe on CCR[2]
  // Probe on CCR[3]
  // Probe on CCR_O[3]
  Multiplexer #(.select(5)) multiplexer_3 (
    .in0(main_2_p4), .in1(main_2_p4), .in2(main_2_p4), .in3(main_2_p4), .in4(main_2_p4), .in5(main_2_p4),
    .in6(main_2_p4), .in8(main_1_p6), .in9(main_1_p6), .in10(main_1_p6), .in11(main_1_p6), .in12(main_1_p6),
    .in13(main_1_p6), .in14(main_1_p6), .in15(main_1_p6), .in16(aritmetic_unit_16_bit_1_p5),
    .in17(aritmetic_unit_16_bit_1_p5), .in18(aritmetic_unit_16_bit_1_p5), .in19(aritmetic_unit_16_bit_1_p5),
    .in20(aritmetic_unit_16_bit_1_p5), .in21(aritmetic_unit_16_bit_1_p5), .in22(aritmetic_unit_16_bit_1_p5),
    .in23(aritmetic_unit_16_bit_1_p5), .in28(aritmetic_unit_16_bit_1_p5), .out(CCR_O[3]),
    .sel({register_1_q, CCR[0]}));  // open: in7, in24, in25, in26, in27, in29, in30, in31, en
  Multiplexer #(.select(5)) multiplexer_4 (
    .in0(main_2_p7), .in1(main_2_p7), .in2(main_2_p7), .in3(main_2_p7), .in4(main_2_p7), .in5(main_2_p7),
    .in6(main_2_p7), .in8(1'b0), .in9(1'b0), .in10(1'b0), .in11(1'b0), .in12(1'b0), .in13(1'b0), .in14(1'b0),
    .in15(1'b0), .in16(aritmetic_unit_16_bit_1_p9), .in17(aritmetic_unit_16_bit_1_p9),
    .in18(aritmetic_unit_16_bit_1_p9), .in19(aritmetic_unit_16_bit_1_p9), .in20(aritmetic_unit_16_bit_1_p9),
    .in21(aritmetic_unit_16_bit_1_p9), .in22(aritmetic_unit_16_bit_1_p9), .in23(aritmetic_unit_16_bit_1_p9),
    .in28(aritmetic_unit_16_bit_1_p9), .out(CCR_O[1]), .sel({register_1_q, CCR[0]}));  // open: in7, in24, in25, in26, in27, in29, in30, in31, en
  // Probe on CCR_O[1]

  assign CCR_O[7:4] = CCR[7:4];

  // Notes on the sheet:
  //   negative flag
  //   zero flag
  //   overflow flag
endmodule
