// Logisim project partb.circ as structural Verilog: 1 circuit, main circuit main
module main (
  input  [15:0] in_1,
  input  [15:0] in_2,
  input  [3:0] in_3,
  output [15:0] out_4
);

  wire clock_1_out;
  wire [7:0] main_1_ccr_o, main_2_p4;

  ALU_main main_1 (.A(in_1), .B(in_2), .Select_Bits(in_3), .CCR(main_2_p4), .out_5(out_4), .CCR_O(main_1_ccr_o));
  Clock clock_1 (.out(clock_1_out));
  // _8_bit_register_main main_2: pin names not known; wires that end beside it: main_1_ccr_o, clock_1_out, 1'b1, main_2_p4
  // Probe on main_2_p4
endmodule
